// Logisim project bladeprod.circ as structural Verilog: 7 circuits, main circuit fullproduct
// 3d_product
module fullproduct (
  input  [31:0] Coefficient_e1a,
  input  [31:0] Coefficient_e2a,
  input  [31:0] Coefficient_e12a,
  input  [31:0] Coefficient_e3a,
  input  [31:0] Coefficient_e31a,
  input  [31:0] Coefficient_e23a,
  input  [31:0] Coefficient_e123a,
  input  [31:0] Coefficient_e0a,
  input  [31:0] Coefficient_e0a_2,
  input  [31:0] Coefficient_e1a_2,
  input  [31:0] Coefficient_e2a_2,
  input  [31:0] Coefficient_e12a_2,
  input  [31:0] Coefficient_e3a_2,
  input  [31:0] Coefficient_e31a_2,
  input  [31:0] Coefficient_e23a_2,
  input  [31:0] Coefficient_e123a_2
);

  wire [2:0] blademult_57_blade_out, blademult_58_blade_out, blademult_59_blade_out, blademult_60_blade_out,
       blademult_61_blade_out, blademult_62_blade_out, blademult_63_blade_out, blademult_64_blade_out;
  wire [3:0] decimalconvert_display_1_digit_1, decimalconvert_display_1_digit_10,
       decimalconvert_display_1_out_3, decimalconvert_display_1_out_4, decimalconvert_display_1_out_5,
       decimalconvert_display_1_out_6, decimalconvert_display_1_out_7, decimalconvert_display_1_out_8,
       decimalconvert_display_1_out_9, decimalconvert_display_1_out_10, decimalconvert_display_2_digit_1,
       decimalconvert_display_2_digit_10, decimalconvert_display_2_out_3, decimalconvert_display_2_out_4,
       decimalconvert_display_2_out_5, decimalconvert_display_2_out_6, decimalconvert_display_2_out_7,
       decimalconvert_display_2_out_8, decimalconvert_display_2_out_9, decimalconvert_display_2_out_10,
       decimalconvert_display_3_digit_1, decimalconvert_display_3_digit_10, decimalconvert_display_3_out_3,
       decimalconvert_display_3_out_4, decimalconvert_display_3_out_5, decimalconvert_display_3_out_6,
       decimalconvert_display_3_out_7, decimalconvert_display_3_out_8, decimalconvert_display_3_out_9,
       decimalconvert_display_3_out_10, decimalconvert_display_4_digit_1, decimalconvert_display_4_digit_10,
       decimalconvert_display_4_out_3, decimalconvert_display_4_out_4, decimalconvert_display_4_out_5,
       decimalconvert_display_4_out_6, decimalconvert_display_4_out_7, decimalconvert_display_4_out_8,
       decimalconvert_display_4_out_9, decimalconvert_display_4_out_10, decimalconvert_display_5_digit_1,
       decimalconvert_display_5_digit_10, decimalconvert_display_5_out_3, decimalconvert_display_5_out_4,
       decimalconvert_display_5_out_5, decimalconvert_display_5_out_6, decimalconvert_display_5_out_7,
       decimalconvert_display_5_out_8, decimalconvert_display_5_out_9, decimalconvert_display_5_out_10,
       decimalconvert_display_6_digit_1, decimalconvert_display_6_digit_10, decimalconvert_display_6_out_3,
       decimalconvert_display_6_out_4, decimalconvert_display_6_out_5, decimalconvert_display_6_out_6,
       decimalconvert_display_6_out_7, decimalconvert_display_6_out_8, decimalconvert_display_6_out_9,
       decimalconvert_display_6_out_10, decimalconvert_display_7_digit_1, decimalconvert_display_7_digit_10,
       decimalconvert_display_7_out_3, decimalconvert_display_7_out_4, decimalconvert_display_7_out_5,
       decimalconvert_display_7_out_6, decimalconvert_display_7_out_7, decimalconvert_display_7_out_8,
       decimalconvert_display_7_out_9, decimalconvert_display_7_out_10, decimalconvert_display_8_digit_1,
       decimalconvert_display_8_digit_10, decimalconvert_display_8_out_3, decimalconvert_display_8_out_4,
       decimalconvert_display_8_out_5, decimalconvert_display_8_out_6, decimalconvert_display_8_out_7,
       decimalconvert_display_8_out_8, decimalconvert_display_8_out_9, decimalconvert_display_8_out_10,
       multiplexer_1_out, multiplexer_1_out_2, multiplexer_1_out_3, multiplexer_1_out_4, multiplexer_1_out_5,
       multiplexer_1_out_6, multiplexer_2_out, multiplexer_2_out_2, multiplexer_2_out_4, multiplexer_2_out_5,
       multiplexer_2_out_6, multiplexer_3_out, multiplexer_3_out_2, multiplexer_3_out_4, multiplexer_3_out_5,
       multiplexer_3_out_6, multiplexer_4_out, multiplexer_4_out_2, multiplexer_4_out_3, multiplexer_4_out_4,
       multiplexer_4_out_5, multiplexer_4_out_6, multiplexer_5_out, multiplexer_5_out_2, multiplexer_5_out_3,
       multiplexer_5_out_4, multiplexer_5_out_5, multiplexer_5_out_6, multiplexer_6_out, multiplexer_6_out_2,
       multiplexer_6_out_4, multiplexer_6_out_5, multiplexer_6_out_6, multiplexer_7_out, multiplexer_7_out_2,
       multiplexer_7_out_3, multiplexer_7_out_4, multiplexer_7_out_5, multiplexer_7_out_6, multiplexer_8_out,
       multiplexer_8_out_2, multiplexer_8_out_4, multiplexer_8_out_5, multiplexer_8_out_6;
  wire [11:8] multiplexer_2_out_3, multiplexer_3_out_3, multiplexer_6_out_3, multiplexer_8_out_3;
  wire [30:0] adder_49_out_2, adder_50_out, adder_52_out;
  wire [31:0] adder_1_out, adder_2_out, adder_3_out, adder_4_out, adder_5_out, adder_6_out, adder_7_out,
       adder_8_out, adder_9_out, adder_10_out, adder_11_out, adder_12_out, adder_13_out, adder_14_out,
       adder_15_out, adder_16_out, adder_17_out, adder_18_out, adder_19_out, adder_20_out, adder_21_out,
       adder_22_out, adder_23_out, adder_24_out, adder_25_out, adder_26_out, adder_27_out, adder_28_out,
       adder_29_out, adder_30_out, adder_31_out, adder_32_out, adder_33_out, adder_34_out, adder_35_out,
       adder_36_out, adder_37_out, adder_38_out, adder_39_out, adder_40_out, adder_41_out, adder_42_out,
       adder_43_out, adder_44_out, adder_45_out, adder_46_out, adder_47_out, adder_48_out, adder_51_out,
       adder_53_out, adder_54_out, adder_55_out, adder_56_out, blademult_1_coefficient_out,
       blademult_2_coefficient_out, blademult_3_coefficient_out, blademult_4_coefficient_out,
       blademult_5_coefficient_out, blademult_6_coefficient_out, blademult_7_coefficient_out,
       blademult_8_coefficient_out, blademult_9_coefficient_out, blademult_10_coefficient_out,
       blademult_11_coefficient_out, blademult_12_coefficient_out, blademult_13_coefficient_out,
       blademult_14_coefficient_out, blademult_15_coefficient_out, blademult_16_coefficient_out,
       blademult_17_coefficient_out, blademult_18_coefficient_out, blademult_19_coefficient_out,
       blademult_20_coefficient_out, blademult_21_coefficient_out, blademult_22_coefficient_out,
       blademult_23_coefficient_out, blademult_24_coefficient_out, blademult_25_coefficient_out,
       blademult_26_coefficient_out, blademult_27_coefficient_out, blademult_28_coefficient_out,
       blademult_29_coefficient_out, blademult_30_coefficient_out, blademult_31_coefficient_out,
       blademult_32_coefficient_out, blademult_33_coefficient_out, blademult_34_coefficient_out,
       blademult_35_coefficient_out, blademult_36_coefficient_out, blademult_37_coefficient_out,
       blademult_38_coefficient_out, blademult_39_coefficient_out, blademult_40_coefficient_out,
       blademult_41_coefficient_out, blademult_42_coefficient_out, blademult_43_coefficient_out,
       blademult_44_coefficient_out, blademult_45_coefficient_out, blademult_46_coefficient_out,
       blademult_47_coefficient_out, blademult_48_coefficient_out, blademult_49_coefficient_out,
       blademult_50_coefficient_out, blademult_51_coefficient_out, blademult_52_coefficient_out,
       blademult_53_coefficient_out, blademult_54_coefficient_out, blademult_55_coefficient_out,
       blademult_56_coefficient_out, blademult_57_coefficient_out, blademult_58_coefficient_out,
       blademult_59_coefficient_out, blademult_60_coefficient_out, blademult_61_coefficient_out,
       blademult_62_coefficient_out, blademult_63_coefficient_out, blademult_64_coefficient_out;
  wire [31:31] adder_49_out, adder_50_out_2, adder_52_out_2;

  _7_Segment_Display u_7_segment_display_1 (.g(adder_49_out[31]));  // open: f, a, b, e, d, c, dp
  Hex_Digit_Display hex_digit_display_1 (.value(decimalconvert_display_1_digit_10));  // open: dp
  decimalconvert_display decimalconvert_display_1 (
    .Signed_Integer({adder_49_out[31], adder_49_out_2}), .digit_10(decimalconvert_display_1_digit_10),
    .out_3(decimalconvert_display_1_out_3), .out_4(decimalconvert_display_1_out_4),
    .out_5(decimalconvert_display_1_out_5), .out_6(decimalconvert_display_1_out_6),
    .out_7(decimalconvert_display_1_out_7), .out_8(decimalconvert_display_1_out_8),
    .out_9(decimalconvert_display_1_out_9), .out_10(decimalconvert_display_1_out_10),
    .digit_1(decimalconvert_display_1_digit_1));
  Hex_Digit_Display hex_digit_display_2 (.value(decimalconvert_display_1_out_3));  // open: dp
  Hex_Digit_Display hex_digit_display_3 (.value(decimalconvert_display_1_out_4));  // open: dp
  Hex_Digit_Display hex_digit_display_4 (.value(decimalconvert_display_1_out_5));  // open: dp
  Hex_Digit_Display hex_digit_display_5 (.value(decimalconvert_display_1_out_6));  // open: dp
  Hex_Digit_Display hex_digit_display_6 (.value(decimalconvert_display_1_out_7));  // open: dp
  Hex_Digit_Display hex_digit_display_7 (.value(decimalconvert_display_1_out_8));  // open: dp
  Hex_Digit_Display hex_digit_display_8 (.value(decimalconvert_display_1_out_9));  // open: dp
  Hex_Digit_Display hex_digit_display_9 (.value(decimalconvert_display_1_out_10));  // open: dp
  Hex_Digit_Display hex_digit_display_10 (.value(decimalconvert_display_1_digit_1));  // open: dp
  blademult blademult_1 (
    .Blade_1(3'b000), .Blade_2(3'b000), .Coefficient_1(Coefficient_e0a), .Coefficient_2(Coefficient_e0a_2),
    .Coefficient_Out(blademult_1_coefficient_out));  // open: Overflow, Blade_Out
  blademult blademult_2 (
    .Blade_1(3'b000), .Blade_2(3'b001), .Coefficient_1(Coefficient_e0a), .Coefficient_2(Coefficient_e1a_2),
    .Coefficient_Out(blademult_2_coefficient_out));  // open: Overflow, Blade_Out
  blademult blademult_3 (
    .Blade_1(3'b000), .Blade_2(3'b010), .Coefficient_1(Coefficient_e0a), .Coefficient_2(Coefficient_e2a_2),
    .Coefficient_Out(blademult_3_coefficient_out));  // open: Overflow, Blade_Out
  blademult blademult_4 (
    .Blade_1(3'b000), .Blade_2(3'b011), .Coefficient_1(Coefficient_e0a), .Coefficient_2(Coefficient_e12a_2),
    .Coefficient_Out(blademult_4_coefficient_out));  // open: Overflow, Blade_Out
  blademult blademult_5 (
    .Blade_1(3'b000), .Blade_2(3'b100), .Coefficient_1(Coefficient_e0a), .Coefficient_2(Coefficient_e3a_2),
    .Coefficient_Out(blademult_5_coefficient_out));  // open: Overflow, Blade_Out
  blademult blademult_6 (
    .Blade_1(3'b000), .Blade_2(3'b101), .Coefficient_1(Coefficient_e0a), .Coefficient_2(Coefficient_e31a_2),
    .Coefficient_Out(blademult_6_coefficient_out));  // open: Overflow, Blade_Out
  blademult blademult_7 (
    .Blade_1(3'b000), .Blade_2(3'b110), .Coefficient_1(Coefficient_e0a), .Coefficient_2(Coefficient_e23a_2),
    .Coefficient_Out(blademult_7_coefficient_out));  // open: Overflow, Blade_Out
  blademult blademult_8 (
    .Blade_1(3'b000), .Blade_2(3'b111), .Coefficient_1(Coefficient_e0a), .Coefficient_2(Coefficient_e123a_2),
    .Coefficient_Out(blademult_8_coefficient_out));  // open: Overflow, Blade_Out
  _7_Segment_Display u_7_segment_display_2 (
    .g(1'b1), .f(1'b1), .a(1'b1), .b(1'b1), .e(1'b1), .d(1'b1), .c(1'b0), .dp(1'b0));
  _7_Segment_Display u_7_segment_display_3 (
    .g(multiplexer_1_out_6[3]), .f(multiplexer_1_out_6[2]), .a(multiplexer_1_out_6[1]),
    .b(multiplexer_1_out_6[0]), .e(multiplexer_1_out_5[3]), .d(multiplexer_1_out_5[2]),
    .c(multiplexer_1_out_5[1]), .dp(multiplexer_1_out_5[0]));
  Multiplexer #(.select(3), .width(24), .enable("false")) multiplexer_1 (
    .in0({24{1'b0}}), .in1(24'h120000), .in2(24'hbc0000), .in3(24'h12bc00), .in4(24'hb60000),
    .in5(24'hb61200), .in6(24'hbcb600), .in7(24'h12bcb6),
    .out({multiplexer_1_out_6, multiplexer_1_out_5, multiplexer_1_out_4, multiplexer_1_out_3, multiplexer_1_out_2, multiplexer_1_out}),
    .sel(blademult_64_blade_out));
  _7_Segment_Display u_7_segment_display_4 (
    .g(multiplexer_1_out_2[3]), .f(multiplexer_1_out_2[2]), .a(multiplexer_1_out_2[1]),
    .b(multiplexer_1_out_2[0]), .e(multiplexer_1_out[3]), .d(multiplexer_1_out[2]), .c(multiplexer_1_out[1]),
    .dp(multiplexer_1_out[0]));
  _7_Segment_Display u_7_segment_display_5 (
    .g(multiplexer_1_out_4[3]), .f(multiplexer_1_out_4[2]), .a(multiplexer_1_out_4[1]),
    .b(multiplexer_1_out_4[0]), .e(multiplexer_1_out_3[3]), .d(multiplexer_1_out_3[2]),
    .c(multiplexer_1_out_3[1]), .dp(multiplexer_1_out_3[0]));
  _7_Segment_Display u_7_segment_display_6 (.g(adder_50_out_2[31]));  // open: f, a, b, e, d, c, dp
  Hex_Digit_Display hex_digit_display_11 (.value(decimalconvert_display_2_digit_10));  // open: dp
  decimalconvert_display decimalconvert_display_2 (
    .Signed_Integer({adder_50_out_2[31], adder_50_out}), .digit_10(decimalconvert_display_2_digit_10),
    .out_3(decimalconvert_display_2_out_3), .out_4(decimalconvert_display_2_out_4),
    .out_5(decimalconvert_display_2_out_5), .out_6(decimalconvert_display_2_out_6),
    .out_7(decimalconvert_display_2_out_7), .out_8(decimalconvert_display_2_out_8),
    .out_9(decimalconvert_display_2_out_9), .out_10(decimalconvert_display_2_out_10),
    .digit_1(decimalconvert_display_2_digit_1));
  Hex_Digit_Display hex_digit_display_12 (.value(decimalconvert_display_2_out_3));  // open: dp
  blademult blademult_9 (
    .Blade_1(3'b001), .Blade_2(3'b000), .Coefficient_1(Coefficient_e1a), .Coefficient_2(Coefficient_e0a_2),
    .Coefficient_Out(blademult_9_coefficient_out));  // open: Overflow, Blade_Out
  blademult blademult_10 (
    .Blade_1(3'b001), .Blade_2(3'b001), .Coefficient_1(Coefficient_e1a), .Coefficient_2(Coefficient_e1a_2),
    .Coefficient_Out(blademult_10_coefficient_out));  // open: Overflow, Blade_Out
  blademult blademult_11 (
    .Blade_1(3'b001), .Blade_2(3'b010), .Coefficient_1(Coefficient_e1a), .Coefficient_2(Coefficient_e2a_2),
    .Coefficient_Out(blademult_11_coefficient_out));  // open: Overflow, Blade_Out
  blademult blademult_12 (
    .Blade_1(3'b001), .Blade_2(3'b011), .Coefficient_1(Coefficient_e1a), .Coefficient_2(Coefficient_e12a_2),
    .Coefficient_Out(blademult_12_coefficient_out));  // open: Overflow, Blade_Out
  blademult blademult_13 (
    .Blade_1(3'b001), .Blade_2(3'b100), .Coefficient_1(Coefficient_e1a), .Coefficient_2(Coefficient_e3a_2),
    .Coefficient_Out(blademult_13_coefficient_out));  // open: Overflow, Blade_Out
  blademult blademult_14 (
    .Blade_1(3'b001), .Blade_2(3'b101), .Coefficient_1(Coefficient_e1a), .Coefficient_2(Coefficient_e31a_2),
    .Coefficient_Out(blademult_14_coefficient_out));  // open: Overflow, Blade_Out
  blademult blademult_15 (
    .Blade_1(3'b001), .Blade_2(3'b110), .Coefficient_1(Coefficient_e1a), .Coefficient_2(Coefficient_e23a_2),
    .Coefficient_Out(blademult_15_coefficient_out));  // open: Overflow, Blade_Out
  blademult blademult_16 (
    .Blade_1(3'b001), .Blade_2(3'b111), .Coefficient_1(Coefficient_e1a), .Coefficient_2(Coefficient_e123a_2),
    .Coefficient_Out(blademult_16_coefficient_out));  // open: Overflow, Blade_Out
  Hex_Digit_Display hex_digit_display_13 (.value(decimalconvert_display_2_out_4));  // open: dp
  Hex_Digit_Display hex_digit_display_14 (.value(decimalconvert_display_2_out_5));  // open: dp
  Hex_Digit_Display hex_digit_display_15 (.value(decimalconvert_display_2_out_6));  // open: dp
  Hex_Digit_Display hex_digit_display_16 (.value(decimalconvert_display_2_out_7));  // open: dp
  Hex_Digit_Display hex_digit_display_17 (.value(decimalconvert_display_2_out_9));  // open: dp
  Hex_Digit_Display hex_digit_display_18 (.value(decimalconvert_display_2_out_8));  // open: dp
  Hex_Digit_Display hex_digit_display_19 (.value(decimalconvert_display_2_out_10));  // open: dp
  Hex_Digit_Display hex_digit_display_20 (.value(decimalconvert_display_2_digit_1));  // open: dp
  Adder #(.width(32)) adder_1 (
    .a(blademult_1_coefficient_out), .b(blademult_10_coefficient_out), .out(adder_1_out));  // open: cin, cout
  Adder #(.width(32)) adder_2 (
    .a(blademult_2_coefficient_out), .b(blademult_9_coefficient_out), .out(adder_2_out));  // open: cin, cout
  Adder #(.width(32)) adder_3 (
    .a(blademult_3_coefficient_out), .b(blademult_12_coefficient_out), .out(adder_3_out));  // open: cin, cout
  Adder #(.width(32)) adder_4 (
    .a(blademult_4_coefficient_out), .b(blademult_11_coefficient_out), .out(adder_4_out));  // open: cin, cout
  Adder #(.width(32)) adder_5 (
    .a(blademult_5_coefficient_out), .b(blademult_14_coefficient_out), .out(adder_5_out));  // open: cin, cout
  Adder #(.width(32)) adder_6 (
    .a(blademult_6_coefficient_out), .b(blademult_13_coefficient_out), .out(adder_6_out));  // open: cin, cout
  Adder #(.width(32)) adder_7 (
    .a(blademult_7_coefficient_out), .b(blademult_16_coefficient_out), .out(adder_7_out));  // open: cin, cout
  Adder #(.width(32)) adder_8 (
    .a(blademult_8_coefficient_out), .b(blademult_15_coefficient_out), .out(adder_8_out));  // open: cin, cout
  _7_Segment_Display u_7_segment_display_7 (
    .g(1'b1), .f(1'b1), .a(1'b1), .b(1'b1), .e(1'b1), .d(1'b1), .c(1'b0), .dp(1'b0));
  _7_Segment_Display u_7_segment_display_8 (
    .g(multiplexer_2_out_6[3]), .f(multiplexer_2_out_6[2]), .a(multiplexer_2_out_6[1]),
    .b(multiplexer_2_out_6[0]), .e(multiplexer_2_out_5[3]), .d(multiplexer_2_out_5[2]),
    .c(multiplexer_2_out_5[1]), .dp(multiplexer_2_out_5[0]));
  _7_Segment_Display u_7_segment_display_9 (
    .g(multiplexer_2_out_4[3]), .f(multiplexer_2_out_4[2]), .a(multiplexer_2_out_4[1]),
    .b(multiplexer_2_out_4[0]), .e(multiplexer_2_out_3[11]), .d(multiplexer_2_out_3[10]),
    .c(multiplexer_2_out_3[9]), .dp(multiplexer_2_out_3[8]));
  blademult blademult_17 (
    .Blade_1(3'b010), .Blade_2(3'b000), .Coefficient_1(Coefficient_e2a), .Coefficient_2(Coefficient_e0a_2),
    .Coefficient_Out(blademult_17_coefficient_out));  // open: Overflow, Blade_Out
  blademult blademult_18 (
    .Blade_1(3'b010), .Blade_2(3'b001), .Coefficient_1(Coefficient_e2a), .Coefficient_2(Coefficient_e1a_2),
    .Coefficient_Out(blademult_18_coefficient_out));  // open: Overflow, Blade_Out
  blademult blademult_19 (
    .Blade_1(3'b010), .Blade_2(3'b010), .Coefficient_1(Coefficient_e2a), .Coefficient_2(Coefficient_e2a_2),
    .Coefficient_Out(blademult_19_coefficient_out));  // open: Overflow, Blade_Out
  blademult blademult_20 (
    .Blade_1(3'b010), .Blade_2(3'b011), .Coefficient_1(Coefficient_e2a), .Coefficient_2(Coefficient_e12a_2),
    .Coefficient_Out(blademult_20_coefficient_out));  // open: Overflow, Blade_Out
  blademult blademult_21 (
    .Blade_1(3'b010), .Blade_2(3'b100), .Coefficient_1(Coefficient_e2a), .Coefficient_2(Coefficient_e3a_2),
    .Coefficient_Out(blademult_21_coefficient_out));  // open: Overflow, Blade_Out
  blademult blademult_22 (
    .Blade_1(3'b010), .Blade_2(3'b101), .Coefficient_1(Coefficient_e2a), .Coefficient_2(Coefficient_e31a_2),
    .Coefficient_Out(blademult_22_coefficient_out));  // open: Overflow, Blade_Out
  blademult blademult_23 (
    .Blade_1(3'b010), .Blade_2(3'b110), .Coefficient_1(Coefficient_e2a), .Coefficient_2(Coefficient_e23a_2),
    .Coefficient_Out(blademult_23_coefficient_out));  // open: Overflow, Blade_Out
  blademult blademult_24 (
    .Blade_1(3'b010), .Blade_2(3'b111), .Coefficient_1(Coefficient_e2a), .Coefficient_2(Coefficient_e123a_2),
    .Coefficient_Out(blademult_24_coefficient_out));  // open: Overflow, Blade_Out
  Multiplexer #(.select(3), .width(24), .enable("false")) multiplexer_2 (
    .in0({24{1'b0}}), .in1(24'h120000), .in2(24'hbc0000), .in3(24'h12bc00), .in4(24'hb60000),
    .in5(24'hb61200), .in6(24'hbcb600), .in7(24'h12bcb6),
    .out({multiplexer_2_out_6, multiplexer_2_out_5, multiplexer_2_out_4, multiplexer_2_out_3, multiplexer_2_out_2, multiplexer_2_out}),
    .sel(blademult_63_blade_out));
  _7_Segment_Display u_7_segment_display_10 (
    .g(multiplexer_2_out_2[3]), .f(multiplexer_2_out_2[2]), .a(multiplexer_2_out_2[1]),
    .b(multiplexer_2_out_2[0]), .e(multiplexer_2_out[3]), .d(multiplexer_2_out[2]), .c(multiplexer_2_out[1]),
    .dp(multiplexer_2_out[0]));
  _7_Segment_Display u_7_segment_display_11 (.g(adder_51_out[31]));  // open: f, a, b, e, d, c, dp
  Hex_Digit_Display hex_digit_display_21 (.value(decimalconvert_display_3_digit_10));  // open: dp
  decimalconvert_display decimalconvert_display_3 (
    .Signed_Integer(adder_51_out), .digit_10(decimalconvert_display_3_digit_10),
    .out_3(decimalconvert_display_3_out_3), .out_4(decimalconvert_display_3_out_4),
    .out_5(decimalconvert_display_3_out_5), .out_6(decimalconvert_display_3_out_6),
    .out_7(decimalconvert_display_3_out_7), .out_8(decimalconvert_display_3_out_8),
    .out_9(decimalconvert_display_3_out_9), .out_10(decimalconvert_display_3_out_10),
    .digit_1(decimalconvert_display_3_digit_1));
  Hex_Digit_Display hex_digit_display_22 (.value(decimalconvert_display_3_out_3));  // open: dp
  Hex_Digit_Display hex_digit_display_23 (.value(decimalconvert_display_3_out_5));  // open: dp
  Hex_Digit_Display hex_digit_display_24 (.value(decimalconvert_display_3_out_4));  // open: dp
  Adder #(.width(32)) adder_9 (
    .a(blademult_19_coefficient_out), .b(adder_1_out), .out(adder_9_out));  // open: cin, cout
  Adder #(.width(32)) adder_10 (
    .a(blademult_20_coefficient_out), .b(adder_2_out), .out(adder_10_out));  // open: cin, cout
  Adder #(.width(32)) adder_11 (
    .a(blademult_17_coefficient_out), .b(adder_3_out), .out(adder_11_out));  // open: cin, cout
  Adder #(.width(32)) adder_12 (
    .a(blademult_18_coefficient_out), .b(adder_4_out), .out(adder_12_out));  // open: cin, cout
  Adder #(.width(32)) adder_13 (
    .a(blademult_23_coefficient_out), .b(adder_5_out), .out(adder_13_out));  // open: cin, cout
  Adder #(.width(32)) adder_14 (
    .a(blademult_24_coefficient_out), .b(adder_6_out), .out(adder_14_out));  // open: cin, cout
  Adder #(.width(32)) adder_15 (
    .a(blademult_21_coefficient_out), .b(adder_7_out), .out(adder_15_out));  // open: cin, cout
  Adder #(.width(32)) adder_16 (
    .a(blademult_22_coefficient_out), .b(adder_8_out), .out(adder_16_out));  // open: cin, cout
  Hex_Digit_Display hex_digit_display_25 (.value(decimalconvert_display_3_out_6));  // open: dp
  Hex_Digit_Display hex_digit_display_26 (.value(decimalconvert_display_3_out_7));  // open: dp
  Hex_Digit_Display hex_digit_display_27 (.value(decimalconvert_display_3_out_8));  // open: dp
  Hex_Digit_Display hex_digit_display_28 (.value(decimalconvert_display_3_out_9));  // open: dp
  Hex_Digit_Display hex_digit_display_29 (.value(decimalconvert_display_3_out_10));  // open: dp
  blademult blademult_25 (
    .Blade_2(3'b000), .Coefficient_1(Coefficient_e12a), .Coefficient_2(Coefficient_e0a_2),
    .Coefficient_Out(blademult_25_coefficient_out));  // open: Blade_1, Overflow, Blade_Out
  blademult blademult_26 (
    .Blade_1(3'b011), .Blade_2(3'b001), .Coefficient_1(Coefficient_e12a), .Coefficient_2(Coefficient_e1a_2),
    .Coefficient_Out(blademult_26_coefficient_out));  // open: Overflow, Blade_Out
  blademult blademult_27 (
    .Blade_1(3'b011), .Blade_2(3'b010), .Coefficient_1(Coefficient_e12a), .Coefficient_2(Coefficient_e2a_2),
    .Coefficient_Out(blademult_27_coefficient_out));  // open: Overflow, Blade_Out
  blademult blademult_28 (
    .Blade_1(3'b011), .Blade_2(3'b011), .Coefficient_1(Coefficient_e12a), .Coefficient_2(Coefficient_e12a_2),
    .Coefficient_Out(blademult_28_coefficient_out));  // open: Overflow, Blade_Out
  blademult blademult_29 (
    .Blade_1(3'b011), .Blade_2(3'b100), .Coefficient_1(Coefficient_e12a), .Coefficient_2(Coefficient_e3a_2),
    .Coefficient_Out(blademult_29_coefficient_out));  // open: Overflow, Blade_Out
  blademult blademult_30 (
    .Blade_1(3'b011), .Blade_2(3'b101), .Coefficient_1(Coefficient_e12a), .Coefficient_2(Coefficient_e31a_2),
    .Coefficient_Out(blademult_30_coefficient_out));  // open: Overflow, Blade_Out
  blademult blademult_31 (
    .Blade_1(3'b011), .Blade_2(3'b110), .Coefficient_1(Coefficient_e12a), .Coefficient_2(Coefficient_e23a_2),
    .Coefficient_Out(blademult_31_coefficient_out));  // open: Overflow, Blade_Out
  blademult blademult_32 (
    .Blade_1(3'b011), .Blade_2(3'b111), .Coefficient_1(Coefficient_e12a),
    .Coefficient_2(Coefficient_e123a_2), .Coefficient_Out(blademult_32_coefficient_out));  // open: Overflow, Blade_Out
  Hex_Digit_Display hex_digit_display_30 (.value(decimalconvert_display_3_digit_1));  // open: dp
  _7_Segment_Display u_7_segment_display_12 (
    .g(1'b1), .f(1'b1), .a(1'b1), .b(1'b1), .e(1'b1), .d(1'b1), .c(1'b0), .dp(1'b0));
  _7_Segment_Display u_7_segment_display_13 (
    .g(multiplexer_3_out_4[3]), .f(multiplexer_3_out_4[2]), .a(multiplexer_3_out_4[1]),
    .b(multiplexer_3_out_4[0]), .e(multiplexer_3_out_3[11]), .d(multiplexer_3_out_3[10]),
    .c(multiplexer_3_out_3[9]), .dp(multiplexer_3_out_3[8]));
  _7_Segment_Display u_7_segment_display_14 (
    .g(multiplexer_3_out_6[3]), .f(multiplexer_3_out_6[2]), .a(multiplexer_3_out_6[1]),
    .b(multiplexer_3_out_6[0]), .e(multiplexer_3_out_5[3]), .d(multiplexer_3_out_5[2]),
    .c(multiplexer_3_out_5[1]), .dp(multiplexer_3_out_5[0]));
  Multiplexer #(.select(3), .width(24), .enable("false")) multiplexer_3 (
    .in0({24{1'b0}}), .in1(24'h120000), .in2(24'hbc0000), .in3(24'h12bc00), .in4(24'hb60000),
    .in5(24'hb61200), .in6(24'hbcb600), .in7(24'h12bcb6),
    .out({multiplexer_3_out_6, multiplexer_3_out_5, multiplexer_3_out_4, multiplexer_3_out_3, multiplexer_3_out_2, multiplexer_3_out}),
    .sel(blademult_62_blade_out));
  _7_Segment_Display u_7_segment_display_15 (
    .g(multiplexer_3_out_2[3]), .f(multiplexer_3_out_2[2]), .a(multiplexer_3_out_2[1]),
    .b(multiplexer_3_out_2[0]), .e(multiplexer_3_out[3]), .d(multiplexer_3_out[2]), .c(multiplexer_3_out[1]),
    .dp(multiplexer_3_out[0]));
  _7_Segment_Display u_7_segment_display_16 (.g(adder_52_out_2[31]));  // open: f, a, b, e, d, c, dp
  Adder #(.width(32)) adder_17 (
    .a(blademult_28_coefficient_out), .b(adder_9_out), .out(adder_17_out));  // open: cin, cout
  Adder #(.width(32)) adder_18 (
    .a(blademult_27_coefficient_out), .b(adder_10_out), .out(adder_18_out));  // open: cin, cout
  Adder #(.width(32)) adder_19 (
    .a(blademult_26_coefficient_out), .b(adder_11_out), .out(adder_19_out));  // open: cin, cout
  Adder #(.width(32)) adder_20 (
    .a(blademult_25_coefficient_out), .b(adder_12_out), .out(adder_20_out));  // open: cin, cout
  Adder #(.width(32)) adder_21 (
    .a(blademult_32_coefficient_out), .b(adder_13_out), .out(adder_21_out));  // open: cin, cout
  Adder #(.width(32)) adder_22 (
    .a(blademult_31_coefficient_out), .b(adder_14_out), .out(adder_22_out));  // open: cin, cout
  Adder #(.width(32)) adder_23 (
    .a(blademult_30_coefficient_out), .b(adder_15_out), .out(adder_23_out));  // open: cin, cout
  Adder #(.width(32)) adder_24 (
    .a(blademult_29_coefficient_out), .b(adder_16_out), .out(adder_24_out));  // open: cin, cout
  decimalconvert_display decimalconvert_display_4 (
    .Signed_Integer({adder_52_out_2[31], adder_52_out}), .digit_10(decimalconvert_display_4_digit_10),
    .out_3(decimalconvert_display_4_out_3), .out_4(decimalconvert_display_4_out_4),
    .out_5(decimalconvert_display_4_out_5), .out_6(decimalconvert_display_4_out_6),
    .out_7(decimalconvert_display_4_out_7), .out_8(decimalconvert_display_4_out_8),
    .out_9(decimalconvert_display_4_out_9), .out_10(decimalconvert_display_4_out_10),
    .digit_1(decimalconvert_display_4_digit_1));
  Hex_Digit_Display hex_digit_display_31 (.value(decimalconvert_display_4_digit_10));  // open: dp
  Hex_Digit_Display hex_digit_display_32 (.value(decimalconvert_display_4_out_3));  // open: dp
  Hex_Digit_Display hex_digit_display_33 (.value(decimalconvert_display_4_out_4));  // open: dp
  Hex_Digit_Display hex_digit_display_34 (.value(decimalconvert_display_4_out_5));  // open: dp
  Hex_Digit_Display hex_digit_display_35 (.value(decimalconvert_display_4_out_6));  // open: dp
  blademult blademult_33 (
    .Blade_1(3'b100), .Blade_2(3'b000), .Coefficient_1(Coefficient_e3a), .Coefficient_2(Coefficient_e0a_2),
    .Coefficient_Out(blademult_33_coefficient_out));  // open: Overflow, Blade_Out
  blademult blademult_34 (
    .Blade_1(3'b100), .Blade_2(3'b001), .Coefficient_1(Coefficient_e3a), .Coefficient_2(Coefficient_e1a_2),
    .Coefficient_Out(blademult_34_coefficient_out));  // open: Overflow, Blade_Out
  blademult blademult_35 (
    .Blade_1(3'b100), .Blade_2(3'b010), .Coefficient_1(Coefficient_e3a), .Coefficient_2(Coefficient_e2a_2),
    .Coefficient_Out(blademult_35_coefficient_out));  // open: Overflow, Blade_Out
  blademult blademult_36 (
    .Blade_1(3'b100), .Blade_2(3'b011), .Coefficient_1(Coefficient_e3a), .Coefficient_2(Coefficient_e12a_2),
    .Coefficient_Out(blademult_36_coefficient_out));  // open: Overflow, Blade_Out
  blademult blademult_37 (
    .Blade_1(3'b100), .Blade_2(3'b100), .Coefficient_1(Coefficient_e3a), .Coefficient_2(Coefficient_e3a_2),
    .Coefficient_Out(blademult_37_coefficient_out));  // open: Overflow, Blade_Out
  blademult blademult_38 (
    .Blade_1(3'b100), .Blade_2(3'b101), .Coefficient_1(Coefficient_e3a), .Coefficient_2(Coefficient_e31a_2),
    .Coefficient_Out(blademult_38_coefficient_out));  // open: Overflow, Blade_Out
  blademult blademult_39 (
    .Blade_1(3'b100), .Blade_2(3'b110), .Coefficient_1(Coefficient_e3a), .Coefficient_2(Coefficient_e23a_2),
    .Coefficient_Out(blademult_39_coefficient_out));  // open: Overflow, Blade_Out
  blademult blademult_40 (
    .Blade_1(3'b100), .Blade_2(3'b111), .Coefficient_1(Coefficient_e3a), .Coefficient_2(Coefficient_e123a_2),
    .Coefficient_Out(blademult_40_coefficient_out));  // open: Overflow, Blade_Out
  Hex_Digit_Display hex_digit_display_36 (.value(decimalconvert_display_4_out_8));  // open: dp
  Hex_Digit_Display hex_digit_display_37 (.value(decimalconvert_display_4_out_7));  // open: dp
  Hex_Digit_Display hex_digit_display_38 (.value(decimalconvert_display_4_out_9));  // open: dp
  Hex_Digit_Display hex_digit_display_39 (.value(decimalconvert_display_4_out_10));  // open: dp
  Hex_Digit_Display hex_digit_display_40 (.value(decimalconvert_display_4_digit_1));  // open: dp
  _7_Segment_Display u_7_segment_display_17 (
    .g(1'b1), .f(1'b1), .a(1'b1), .b(1'b1), .e(1'b1), .d(1'b1), .c(1'b0), .dp(1'b0));
  _7_Segment_Display u_7_segment_display_18 (
    .g(multiplexer_4_out_6[3]), .f(multiplexer_4_out_6[2]), .a(multiplexer_4_out_6[1]),
    .b(multiplexer_4_out_6[0]), .e(multiplexer_4_out_5[3]), .d(multiplexer_4_out_5[2]),
    .c(multiplexer_4_out_5[1]), .dp(multiplexer_4_out_5[0]));
  _7_Segment_Display u_7_segment_display_19 (
    .g(multiplexer_4_out_4[3]), .f(multiplexer_4_out_4[2]), .a(multiplexer_4_out_4[1]),
    .b(multiplexer_4_out_4[0]), .e(multiplexer_4_out_3[3]), .d(multiplexer_4_out_3[2]),
    .c(multiplexer_4_out_3[1]), .dp(multiplexer_4_out_3[0]));
  Adder #(.width(32)) adder_25 (
    .a(blademult_37_coefficient_out), .b(adder_17_out), .out(adder_25_out));  // open: cin, cout
  Adder #(.width(32)) adder_26 (
    .a(blademult_38_coefficient_out), .b(adder_18_out), .out(adder_26_out));  // open: cin, cout
  Adder #(.width(32)) adder_27 (
    .a(blademult_39_coefficient_out), .b(adder_19_out), .out(adder_27_out));  // open: cin, cout
  Adder #(.width(32)) adder_28 (
    .a(blademult_40_coefficient_out), .b(adder_20_out), .out(adder_28_out));  // open: cin, cout
  Adder #(.width(32)) adder_29 (
    .a(blademult_33_coefficient_out), .b(adder_21_out), .out(adder_29_out));  // open: cin, cout
  Adder #(.width(32)) adder_30 (
    .a(blademult_34_coefficient_out), .b(adder_22_out), .out(adder_30_out));  // open: cin, cout
  Adder #(.width(32)) adder_31 (
    .a(blademult_35_coefficient_out), .b(adder_23_out), .out(adder_31_out));  // open: cin, cout
  Adder #(.width(32)) adder_32 (
    .a(blademult_36_coefficient_out), .b(adder_24_out), .out(adder_32_out));  // open: cin, cout
  Multiplexer #(.select(3), .width(24), .enable("false")) multiplexer_4 (
    .in0({24{1'b0}}), .in1(24'h120000), .in2(24'hbc0000), .in3(24'h12bc00), .in4(24'hb60000),
    .in5(24'hb61200), .in6(24'hbcb600), .in7(24'h12bcb6),
    .out({multiplexer_4_out_6, multiplexer_4_out_5, multiplexer_4_out_4, multiplexer_4_out_3, multiplexer_4_out_2, multiplexer_4_out}),
    .sel(blademult_61_blade_out));
  _7_Segment_Display u_7_segment_display_20 (
    .g(multiplexer_4_out_2[3]), .f(multiplexer_4_out_2[2]), .a(multiplexer_4_out_2[1]),
    .b(multiplexer_4_out_2[0]), .e(multiplexer_4_out[3]), .d(multiplexer_4_out[2]), .c(multiplexer_4_out[1]),
    .dp(multiplexer_4_out[0]));
  _7_Segment_Display u_7_segment_display_21 (.g(adder_53_out[31]));  // open: f, a, b, e, d, c, dp
  blademult blademult_41 (
    .Blade_1(3'b101), .Blade_2(3'b000), .Coefficient_1(Coefficient_e31a), .Coefficient_2(Coefficient_e0a_2),
    .Coefficient_Out(blademult_41_coefficient_out));  // open: Overflow, Blade_Out
  blademult blademult_42 (
    .Blade_1(3'b101), .Blade_2(3'b001), .Coefficient_1(Coefficient_e31a), .Coefficient_2(Coefficient_e1a_2),
    .Coefficient_Out(blademult_42_coefficient_out));  // open: Overflow, Blade_Out
  blademult blademult_43 (
    .Blade_1(3'b101), .Blade_2(3'b010), .Coefficient_1(Coefficient_e31a), .Coefficient_2(Coefficient_e2a_2),
    .Coefficient_Out(blademult_43_coefficient_out));  // open: Overflow, Blade_Out
  blademult blademult_44 (
    .Blade_1(3'b101), .Blade_2(3'b011), .Coefficient_1(Coefficient_e31a), .Coefficient_2(Coefficient_e12a_2),
    .Coefficient_Out(blademult_44_coefficient_out));  // open: Overflow, Blade_Out
  blademult blademult_45 (
    .Blade_1(3'b101), .Blade_2(3'b100), .Coefficient_1(Coefficient_e31a), .Coefficient_2(Coefficient_e3a_2),
    .Coefficient_Out(blademult_45_coefficient_out));  // open: Overflow, Blade_Out
  blademult blademult_46 (
    .Blade_1(3'b101), .Blade_2(3'b101), .Coefficient_1(Coefficient_e31a), .Coefficient_2(Coefficient_e31a_2),
    .Coefficient_Out(blademult_46_coefficient_out));  // open: Overflow, Blade_Out
  blademult blademult_47 (
    .Blade_1(3'b101), .Blade_2(3'b110), .Coefficient_1(Coefficient_e31a), .Coefficient_2(Coefficient_e23a_2),
    .Coefficient_Out(blademult_47_coefficient_out));  // open: Overflow, Blade_Out
  blademult blademult_48 (
    .Blade_1(3'b101), .Blade_2(3'b111), .Coefficient_1(Coefficient_e31a),
    .Coefficient_2(Coefficient_e123a_2), .Coefficient_Out(blademult_48_coefficient_out));  // open: Overflow, Blade_Out
  decimalconvert_display decimalconvert_display_5 (
    .Signed_Integer(adder_53_out), .digit_10(decimalconvert_display_5_digit_10),
    .out_3(decimalconvert_display_5_out_3), .out_4(decimalconvert_display_5_out_4),
    .out_5(decimalconvert_display_5_out_5), .out_6(decimalconvert_display_5_out_6),
    .out_7(decimalconvert_display_5_out_7), .out_8(decimalconvert_display_5_out_8),
    .out_9(decimalconvert_display_5_out_9), .out_10(decimalconvert_display_5_out_10),
    .digit_1(decimalconvert_display_5_digit_1));
  Hex_Digit_Display hex_digit_display_41 (.value(decimalconvert_display_5_digit_10));  // open: dp
  Hex_Digit_Display hex_digit_display_42 (.value(decimalconvert_display_5_out_3));  // open: dp
  Hex_Digit_Display hex_digit_display_43 (.value(decimalconvert_display_5_out_4));  // open: dp
  Hex_Digit_Display hex_digit_display_44 (.value(decimalconvert_display_5_out_5));  // open: dp
  Hex_Digit_Display hex_digit_display_45 (.value(decimalconvert_display_5_out_6));  // open: dp
  Hex_Digit_Display hex_digit_display_46 (.value(decimalconvert_display_5_out_7));  // open: dp
  Hex_Digit_Display hex_digit_display_47 (.value(decimalconvert_display_5_out_8));  // open: dp
  Adder #(.width(32)) adder_33 (
    .a(blademult_46_coefficient_out), .b(adder_25_out), .out(adder_33_out));  // open: cin, cout
  Adder #(.width(32)) adder_34 (
    .a(blademult_45_coefficient_out), .b(adder_26_out), .out(adder_34_out));  // open: cin, cout
  Adder #(.width(32)) adder_35 (
    .a(blademult_48_coefficient_out), .b(adder_27_out), .out(adder_35_out));  // open: cin, cout
  Adder #(.width(32)) adder_36 (
    .a(blademult_47_coefficient_out), .b(adder_28_out), .out(adder_36_out));  // open: cin, cout
  Adder #(.width(32)) adder_37 (
    .a(blademult_42_coefficient_out), .b(adder_29_out), .out(adder_37_out));  // open: cin, cout
  Adder #(.width(32)) adder_38 (
    .a(blademult_41_coefficient_out), .b(adder_30_out), .out(adder_38_out));  // open: cin, cout
  Adder #(.width(32)) adder_39 (
    .a(blademult_44_coefficient_out), .b(adder_31_out), .out(adder_39_out));  // open: cin, cout
  Adder #(.width(32)) adder_40 (
    .a(blademult_43_coefficient_out), .b(adder_32_out), .out(adder_40_out));  // open: cin, cout
  Hex_Digit_Display hex_digit_display_48 (.value(decimalconvert_display_5_out_9));  // open: dp
  Hex_Digit_Display hex_digit_display_49 (.value(decimalconvert_display_5_out_10));  // open: dp
  Hex_Digit_Display hex_digit_display_50 (.value(decimalconvert_display_5_digit_1));  // open: dp
  _7_Segment_Display u_7_segment_display_22 (
    .g(1'b1), .f(1'b1), .a(1'b1), .b(1'b1), .e(1'b1), .d(1'b1), .c(1'b0), .dp(1'b0));
  _7_Segment_Display u_7_segment_display_23 (
    .g(multiplexer_5_out_6[3]), .f(multiplexer_5_out_6[2]), .a(multiplexer_5_out_6[1]),
    .b(multiplexer_5_out_6[0]), .e(multiplexer_5_out_5[3]), .d(multiplexer_5_out_5[2]),
    .c(multiplexer_5_out_5[1]), .dp(multiplexer_5_out_5[0]));
  blademult blademult_49 (
    .Blade_1(3'b110), .Blade_2(3'b000), .Coefficient_1(Coefficient_e23a), .Coefficient_2(Coefficient_e0a_2),
    .Coefficient_Out(blademult_49_coefficient_out));  // open: Overflow, Blade_Out
  blademult blademult_50 (
    .Blade_1(3'b110), .Blade_2(3'b001), .Coefficient_1(Coefficient_e23a), .Coefficient_2(Coefficient_e1a_2),
    .Coefficient_Out(blademult_50_coefficient_out));  // open: Overflow, Blade_Out
  blademult blademult_51 (
    .Blade_1(3'b110), .Blade_2(3'b010), .Coefficient_1(Coefficient_e23a), .Coefficient_2(Coefficient_e2a_2),
    .Coefficient_Out(blademult_51_coefficient_out));  // open: Overflow, Blade_Out
  blademult blademult_52 (
    .Blade_1(3'b110), .Blade_2(3'b011), .Coefficient_1(Coefficient_e23a), .Coefficient_2(Coefficient_e12a_2),
    .Coefficient_Out(blademult_52_coefficient_out));  // open: Overflow, Blade_Out
  blademult blademult_53 (
    .Blade_1(3'b110), .Blade_2(3'b100), .Coefficient_1(Coefficient_e23a), .Coefficient_2(Coefficient_e3a_2),
    .Coefficient_Out(blademult_53_coefficient_out));  // open: Overflow, Blade_Out
  blademult blademult_54 (
    .Blade_1(3'b110), .Blade_2(3'b101), .Coefficient_1(Coefficient_e23a), .Coefficient_2(Coefficient_e31a_2),
    .Coefficient_Out(blademult_54_coefficient_out));  // open: Overflow, Blade_Out
  blademult blademult_55 (
    .Blade_1(3'b110), .Blade_2(3'b110), .Coefficient_1(Coefficient_e23a), .Coefficient_2(Coefficient_e23a_2),
    .Coefficient_Out(blademult_55_coefficient_out));  // open: Overflow, Blade_Out
  blademult blademult_56 (
    .Blade_1(3'b110), .Blade_2(3'b111), .Coefficient_1(Coefficient_e23a),
    .Coefficient_2(Coefficient_e123a_2), .Coefficient_Out(blademult_56_coefficient_out));  // open: Overflow, Blade_Out
  Multiplexer #(.select(3), .width(24), .enable("false")) multiplexer_5 (
    .in0({24{1'b0}}), .in1(24'h120000), .in2(24'hbc0000), .in3(24'h12bc00), .in4(24'hb60000),
    .in5(24'hb61200), .in6(24'hbcb600), .in7(24'h12bcb6),
    .out({multiplexer_5_out_6, multiplexer_5_out_5, multiplexer_5_out_4, multiplexer_5_out_3, multiplexer_5_out_2, multiplexer_5_out}),
    .sel(blademult_60_blade_out));
  _7_Segment_Display u_7_segment_display_24 (
    .g(multiplexer_5_out_4[3]), .f(multiplexer_5_out_4[2]), .a(multiplexer_5_out_4[1]),
    .b(multiplexer_5_out_4[0]), .e(multiplexer_5_out_3[3]), .d(multiplexer_5_out_3[2]),
    .c(multiplexer_5_out_3[1]), .dp(multiplexer_5_out_3[0]));
  _7_Segment_Display u_7_segment_display_25 (
    .g(multiplexer_5_out_2[3]), .f(multiplexer_5_out_2[2]), .a(multiplexer_5_out_2[1]),
    .b(multiplexer_5_out_2[0]), .e(multiplexer_5_out[3]), .d(multiplexer_5_out[2]), .c(multiplexer_5_out[1]),
    .dp(multiplexer_5_out[0]));
  _7_Segment_Display u_7_segment_display_26 (.g(adder_54_out[31]));  // open: f, a, b, e, d, c, dp
  Hex_Digit_Display hex_digit_display_51 (.value(decimalconvert_display_6_digit_10));  // open: dp
  Adder #(.width(32)) adder_41 (
    .a(blademult_55_coefficient_out), .b(adder_33_out), .out(adder_41_out));  // open: cin, cout
  Adder #(.width(32)) adder_42 (
    .a(blademult_56_coefficient_out), .b(adder_34_out), .out(adder_42_out));  // open: cin, cout
  Adder #(.width(32)) adder_43 (
    .a(blademult_53_coefficient_out), .b(adder_35_out), .out(adder_43_out));  // open: cin, cout
  Adder #(.width(32)) adder_44 (
    .a(blademult_54_coefficient_out), .b(adder_36_out), .out(adder_44_out));  // open: cin, cout
  Adder #(.width(32)) adder_45 (
    .a(blademult_51_coefficient_out), .b(adder_37_out), .out(adder_45_out));  // open: cin, cout
  Adder #(.width(32)) adder_46 (
    .a(blademult_52_coefficient_out), .b(adder_38_out), .out(adder_46_out));  // open: cin, cout
  Adder #(.width(32)) adder_47 (
    .a(blademult_49_coefficient_out), .b(adder_39_out), .out(adder_47_out));  // open: cin, cout
  Adder #(.width(32)) adder_48 (
    .a(blademult_50_coefficient_out), .b(adder_40_out), .out(adder_48_out));  // open: cin, cout
  decimalconvert_display decimalconvert_display_6 (
    .Signed_Integer(adder_54_out), .digit_10(decimalconvert_display_6_digit_10),
    .out_3(decimalconvert_display_6_out_3), .out_4(decimalconvert_display_6_out_4),
    .out_5(decimalconvert_display_6_out_5), .out_6(decimalconvert_display_6_out_6),
    .out_7(decimalconvert_display_6_out_7), .out_8(decimalconvert_display_6_out_8),
    .out_9(decimalconvert_display_6_out_9), .out_10(decimalconvert_display_6_out_10),
    .digit_1(decimalconvert_display_6_digit_1));
  Hex_Digit_Display hex_digit_display_52 (.value(decimalconvert_display_6_out_3));  // open: dp
  Hex_Digit_Display hex_digit_display_53 (.value(decimalconvert_display_6_out_4));  // open: dp
  Hex_Digit_Display hex_digit_display_54 (.value(decimalconvert_display_6_out_5));  // open: dp
  blademult blademult_57 (
    .Blade_1(3'b111), .Blade_2(3'b000), .Coefficient_1(Coefficient_e123a), .Coefficient_2(Coefficient_e0a_2),
    .Blade_Out(blademult_57_blade_out), .Coefficient_Out(blademult_57_coefficient_out));  // open: Overflow
  blademult blademult_58 (
    .Blade_1(3'b111), .Blade_2(3'b001), .Coefficient_1(Coefficient_e123a), .Coefficient_2(Coefficient_e1a_2),
    .Blade_Out(blademult_58_blade_out), .Coefficient_Out(blademult_58_coefficient_out));  // open: Overflow
  blademult blademult_59 (
    .Blade_1(3'b111), .Blade_2(3'b010), .Coefficient_1(Coefficient_e123a), .Coefficient_2(Coefficient_e2a_2),
    .Blade_Out(blademult_59_blade_out), .Coefficient_Out(blademult_59_coefficient_out));  // open: Overflow
  blademult blademult_60 (
    .Blade_1(3'b111), .Blade_2(3'b011), .Coefficient_1(Coefficient_e123a),
    .Coefficient_2(Coefficient_e12a_2), .Blade_Out(blademult_60_blade_out),
    .Coefficient_Out(blademult_60_coefficient_out));  // open: Overflow
  blademult blademult_61 (
    .Blade_1(3'b111), .Blade_2(3'b100), .Coefficient_1(Coefficient_e123a), .Coefficient_2(Coefficient_e3a_2),
    .Blade_Out(blademult_61_blade_out), .Coefficient_Out(blademult_61_coefficient_out));  // open: Overflow
  blademult blademult_62 (
    .Blade_1(3'b111), .Blade_2(3'b101), .Coefficient_1(Coefficient_e123a),
    .Coefficient_2(Coefficient_e31a_2), .Blade_Out(blademult_62_blade_out),
    .Coefficient_Out(blademult_62_coefficient_out));  // open: Overflow
  blademult blademult_63 (
    .Blade_1(3'b111), .Blade_2(3'b110), .Coefficient_1(Coefficient_e123a),
    .Coefficient_2(Coefficient_e23a_2), .Blade_Out(blademult_63_blade_out),
    .Coefficient_Out(blademult_63_coefficient_out));  // open: Overflow
  blademult blademult_64 (
    .Blade_1(3'b111), .Blade_2(3'b111), .Coefficient_1(Coefficient_e123a),
    .Coefficient_2(Coefficient_e123a_2), .Blade_Out(blademult_64_blade_out),
    .Coefficient_Out(blademult_64_coefficient_out));  // open: Overflow
  Hex_Digit_Display hex_digit_display_55 (.value(decimalconvert_display_6_out_6));  // open: dp
  Hex_Digit_Display hex_digit_display_56 (.value(decimalconvert_display_6_out_7));  // open: dp
  Hex_Digit_Display hex_digit_display_57 (.value(decimalconvert_display_6_out_9));  // open: dp
  Hex_Digit_Display hex_digit_display_58 (.value(decimalconvert_display_6_out_8));  // open: dp
  Hex_Digit_Display hex_digit_display_59 (.value(decimalconvert_display_6_out_10));  // open: dp
  Hex_Digit_Display hex_digit_display_60 (.value(decimalconvert_display_6_digit_1));  // open: dp
  _7_Segment_Display u_7_segment_display_27 (
    .g(1'b1), .f(1'b1), .a(1'b1), .b(1'b1), .e(1'b1), .d(1'b1), .c(1'b0), .dp(1'b0));
  Adder #(.width(32)) adder_49 (
    .a(blademult_64_coefficient_out), .b(adder_41_out), .out({adder_49_out[31], adder_49_out_2}));  // open: cin, cout
  Adder #(.width(32)) adder_50 (
    .a(blademult_63_coefficient_out), .b(adder_42_out), .out({adder_50_out_2[31], adder_50_out}));  // open: cin, cout
  Adder #(.width(32)) adder_51 (
    .a(blademult_62_coefficient_out), .b(adder_43_out), .out(adder_51_out));  // open: cin, cout
  Adder #(.width(32)) adder_52 (
    .a(blademult_61_coefficient_out), .b(adder_44_out), .out({adder_52_out_2[31], adder_52_out}));  // open: cin, cout
  Adder #(.width(32)) adder_53 (
    .a(blademult_60_coefficient_out), .b(adder_45_out), .out(adder_53_out));  // open: cin, cout
  Adder #(.width(32)) adder_54 (
    .a(blademult_59_coefficient_out), .b(adder_46_out), .out(adder_54_out));  // open: cin, cout
  Adder #(.width(32)) adder_55 (
    .a(blademult_58_coefficient_out), .b(adder_47_out), .out(adder_55_out));  // open: cin, cout
  Adder #(.width(32)) adder_56 (
    .a(blademult_57_coefficient_out), .b(adder_48_out), .out(adder_56_out));  // open: cin, cout
  _7_Segment_Display u_7_segment_display_28 (
    .g(multiplexer_6_out_4[3]), .f(multiplexer_6_out_4[2]), .a(multiplexer_6_out_4[1]),
    .b(multiplexer_6_out_4[0]), .e(multiplexer_6_out_3[11]), .d(multiplexer_6_out_3[10]),
    .c(multiplexer_6_out_3[9]), .dp(multiplexer_6_out_3[8]));
  _7_Segment_Display u_7_segment_display_29 (
    .g(multiplexer_6_out_6[3]), .f(multiplexer_6_out_6[2]), .a(multiplexer_6_out_6[1]),
    .b(multiplexer_6_out_6[0]), .e(multiplexer_6_out_5[3]), .d(multiplexer_6_out_5[2]),
    .c(multiplexer_6_out_5[1]), .dp(multiplexer_6_out_5[0]));
  Multiplexer #(.select(3), .width(24), .enable("false")) multiplexer_6 (
    .in0({24{1'b0}}), .in1(24'h120000), .in2(24'hbc0000), .in3(24'h12bc00), .in4(24'hb60000),
    .in5(24'hb61200), .in6(24'hbcb600), .in7(24'h12bcb6),
    .out({multiplexer_6_out_6, multiplexer_6_out_5, multiplexer_6_out_4, multiplexer_6_out_3, multiplexer_6_out_2, multiplexer_6_out}),
    .sel(blademult_59_blade_out));
  _7_Segment_Display u_7_segment_display_30 (
    .g(multiplexer_6_out_2[3]), .f(multiplexer_6_out_2[2]), .a(multiplexer_6_out_2[1]),
    .b(multiplexer_6_out_2[0]), .e(multiplexer_6_out[3]), .d(multiplexer_6_out[2]), .c(multiplexer_6_out[1]),
    .dp(multiplexer_6_out[0]));
  _7_Segment_Display u_7_segment_display_31 (.g(adder_55_out[31]));  // open: f, a, b, e, d, c, dp
  Hex_Digit_Display hex_digit_display_61 (.value(decimalconvert_display_7_digit_10));  // open: dp
  decimalconvert_display decimalconvert_display_7 (
    .Signed_Integer(adder_55_out), .digit_10(decimalconvert_display_7_digit_10),
    .out_3(decimalconvert_display_7_out_3), .out_4(decimalconvert_display_7_out_4),
    .out_5(decimalconvert_display_7_out_5), .out_6(decimalconvert_display_7_out_6),
    .out_7(decimalconvert_display_7_out_7), .out_8(decimalconvert_display_7_out_8),
    .out_9(decimalconvert_display_7_out_9), .out_10(decimalconvert_display_7_out_10),
    .digit_1(decimalconvert_display_7_digit_1));
  Hex_Digit_Display hex_digit_display_62 (.value(decimalconvert_display_7_out_3));  // open: dp
  Hex_Digit_Display hex_digit_display_63 (.value(decimalconvert_display_7_out_5));  // open: dp
  Hex_Digit_Display hex_digit_display_64 (.value(decimalconvert_display_7_out_4));  // open: dp
  Hex_Digit_Display hex_digit_display_65 (.value(decimalconvert_display_7_out_6));  // open: dp
  Hex_Digit_Display hex_digit_display_66 (.value(decimalconvert_display_7_out_7));  // open: dp
  Hex_Digit_Display hex_digit_display_67 (.value(decimalconvert_display_7_out_8));  // open: dp
  Hex_Digit_Display hex_digit_display_68 (.value(decimalconvert_display_7_out_9));  // open: dp
  Hex_Digit_Display hex_digit_display_69 (.value(decimalconvert_display_7_out_10));  // open: dp
  Hex_Digit_Display hex_digit_display_70 (.value(decimalconvert_display_7_digit_1));  // open: dp
  _7_Segment_Display u_7_segment_display_32 (
    .g(1'b1), .f(1'b1), .a(1'b1), .b(1'b1), .e(1'b1), .d(1'b1), .c(1'b0), .dp(1'b0));
  _7_Segment_Display u_7_segment_display_33 (
    .g(multiplexer_7_out_6[3]), .f(multiplexer_7_out_6[2]), .a(multiplexer_7_out_6[1]),
    .b(multiplexer_7_out_6[0]), .e(multiplexer_7_out_5[3]), .d(multiplexer_7_out_5[2]),
    .c(multiplexer_7_out_5[1]), .dp(multiplexer_7_out_5[0]));
  _7_Segment_Display u_7_segment_display_34 (
    .g(multiplexer_7_out_4[3]), .f(multiplexer_7_out_4[2]), .a(multiplexer_7_out_4[1]),
    .b(multiplexer_7_out_4[0]), .e(multiplexer_7_out_3[3]), .d(multiplexer_7_out_3[2]),
    .c(multiplexer_7_out_3[1]), .dp(multiplexer_7_out_3[0]));
  Multiplexer #(.select(3), .width(24), .enable("false")) multiplexer_7 (
    .in0({24{1'b0}}), .in1(24'h120000), .in2(24'hbc0000), .in3(24'h12bc00), .in4(24'hb60000),
    .in5(24'hb61200), .in6(24'hbcb600), .in7(24'h12bcb6),
    .out({multiplexer_7_out_6, multiplexer_7_out_5, multiplexer_7_out_4, multiplexer_7_out_3, multiplexer_7_out_2, multiplexer_7_out}),
    .sel(blademult_58_blade_out));
  _7_Segment_Display u_7_segment_display_35 (
    .g(multiplexer_7_out_2[3]), .f(multiplexer_7_out_2[2]), .a(multiplexer_7_out_2[1]),
    .b(multiplexer_7_out_2[0]), .e(multiplexer_7_out[3]), .d(multiplexer_7_out[2]), .c(multiplexer_7_out[1]),
    .dp(multiplexer_7_out[0]));
  _7_Segment_Display u_7_segment_display_36 (.g(adder_56_out[31]));  // open: f, a, b, e, d, c, dp
  decimalconvert_display decimalconvert_display_8 (
    .Signed_Integer(adder_56_out), .digit_10(decimalconvert_display_8_digit_10),
    .out_3(decimalconvert_display_8_out_3), .out_4(decimalconvert_display_8_out_4),
    .out_5(decimalconvert_display_8_out_5), .out_6(decimalconvert_display_8_out_6),
    .out_7(decimalconvert_display_8_out_7), .out_8(decimalconvert_display_8_out_8),
    .out_9(decimalconvert_display_8_out_9), .out_10(decimalconvert_display_8_out_10),
    .digit_1(decimalconvert_display_8_digit_1));
  Hex_Digit_Display hex_digit_display_71 (.value(decimalconvert_display_8_digit_10));  // open: dp
  Hex_Digit_Display hex_digit_display_72 (.value(decimalconvert_display_8_out_3));  // open: dp
  Hex_Digit_Display hex_digit_display_73 (.value(decimalconvert_display_8_out_4));  // open: dp
  Hex_Digit_Display hex_digit_display_74 (.value(decimalconvert_display_8_out_5));  // open: dp
  Hex_Digit_Display hex_digit_display_75 (.value(decimalconvert_display_8_out_6));  // open: dp
  Hex_Digit_Display hex_digit_display_76 (.value(decimalconvert_display_8_out_7));  // open: dp
  Hex_Digit_Display hex_digit_display_77 (.value(decimalconvert_display_8_out_8));  // open: dp
  Hex_Digit_Display hex_digit_display_78 (.value(decimalconvert_display_8_out_9));  // open: dp
  Hex_Digit_Display hex_digit_display_79 (.value(decimalconvert_display_8_out_10));  // open: dp
  Hex_Digit_Display hex_digit_display_80 (.value(decimalconvert_display_8_digit_1));  // open: dp
  _7_Segment_Display u_7_segment_display_37 (
    .g(1'b1), .f(1'b1), .a(1'b1), .b(1'b1), .e(1'b1), .d(1'b1), .c(1'b0), .dp(1'b0));
  _7_Segment_Display u_7_segment_display_38 (
    .g(multiplexer_8_out_6[3]), .f(multiplexer_8_out_6[2]), .a(multiplexer_8_out_6[1]),
    .b(multiplexer_8_out_6[0]), .e(multiplexer_8_out_5[3]), .d(multiplexer_8_out_5[2]),
    .c(multiplexer_8_out_5[1]), .dp(multiplexer_8_out_5[0]));
  _7_Segment_Display u_7_segment_display_39 (
    .g(multiplexer_8_out_4[3]), .f(multiplexer_8_out_4[2]), .a(multiplexer_8_out_4[1]),
    .b(multiplexer_8_out_4[0]), .e(multiplexer_8_out_3[11]), .d(multiplexer_8_out_3[10]),
    .c(multiplexer_8_out_3[9]), .dp(multiplexer_8_out_3[8]));
  Multiplexer #(.select(3), .width(24), .enable("false")) multiplexer_8 (
    .in0({24{1'b0}}), .in1(24'h120000), .in2(24'hbc0000), .in3(24'h12bc00), .in4(24'hb60000),
    .in5(24'hb61200), .in6(24'hbcb600), .in7(24'h12bcb6),
    .out({multiplexer_8_out_6, multiplexer_8_out_5, multiplexer_8_out_4, multiplexer_8_out_3, multiplexer_8_out_2, multiplexer_8_out}),
    .sel(blademult_57_blade_out));
  _7_Segment_Display u_7_segment_display_40 (
    .g(multiplexer_8_out_2[3]), .f(multiplexer_8_out_2[2]), .a(multiplexer_8_out_2[1]),
    .b(multiplexer_8_out_2[0]), .e(multiplexer_8_out[3]), .d(multiplexer_8_out[2]), .c(multiplexer_8_out[1]),
    .dp(multiplexer_8_out[0]));

  // Notes on the sheet:
  //   e123
  //   e23
  //   e31
  //   e3
  //   e12
  //   e2
  //   e1
  //   e0
  //   e123
  //   e23
  //   e31
  //   e3
  //   e12
  //   e2
  //   e1
  //   e0
  //   Addition of Like Terms
  //   e123
  //   e23
  //   e31
  //   e3
  //   e12
  //   e2
  //   e1
  //   e0
  //   e123
  //   e23
  //   e31
  //   e3
  //   e12
  //   e2
  //   e1
  //   e0
  //   e123
  //   e23
  //   e31
  //   e3
  //   e12
  //   e2
  //   e1
  //   e0
  //   e123
  //   e23
  //   e31
  //   e3
  //   e12
  //   e2
  //   e1
  //   e0
  //   e123
  //   e23
  //   e31
  //   e3
  //   e12
  //   e2
  //   e1
  //   e0
  //   e123
  //   e23
  //   e31
  //   e3
  //   e12
  //   e2
  //   e1
  //   e0
endmodule

// blade_multiplier
module blademult (
  input  [2:0] Blade_1,
  input  [2:0] Blade_2,
  input  [31:0] Coefficient_1,
  input  [31:0] Coefficient_2,
  output [2:0] Blade_Out,
  output [31:0] Coefficient_Out,
  output [31:0] Overflow
);

  wire or_1_out, or_2_out, or_3_out;
  wire [3:0] decimalconvert_display_1_digit_1, decimalconvert_display_1_digit_10,
       decimalconvert_display_1_out_3, decimalconvert_display_1_out_4, decimalconvert_display_1_out_5,
       decimalconvert_display_1_out_6, decimalconvert_display_1_out_7, decimalconvert_display_1_out_8,
       decimalconvert_display_1_out_9, decimalconvert_display_1_out_10, multiplexer_3_out,
       multiplexer_3_out_2, multiplexer_3_out_3, multiplexer_3_out_4, multiplexer_3_out_5,
       multiplexer_3_out_6;
  wire [7:0] and_1_out, multiplexer_1_out, multiplexer_2_out;
  wire [31:0] bit_extender_1_out, multiplier_1_out, n32bitxor_1_coefficient;

  Multiplexer #(.select(3), .width(8), .enable("false")) multiplexer_1 (
    .in0({8{1'b0}}), .in1(8'h2), .in2(8'h4), .in3(8'h8), .in4(8'hf), .in5(8'h2), .in6(8'h4), .in7(8'h80),
    .out(multiplexer_1_out), .sel(Blade_2));
  Multiplexer #(.select(3), .width(8), .enable("false")) multiplexer_2 (
    .in0({8{1'b0}}), .in1(8'h30), .in2(8'ha), .in3(8'hca), .in4(8'h44), .in5(8'hb8), .in6(8'he4),
    .in7(8'he8), .out(multiplexer_2_out), .sel(Blade_1));
  assign and_1_out = multiplexer_1_out & multiplexer_2_out;  // AND_Gate and_1, 8 bits wide
  assign bit_extender_1_out = {{31{or_3_out}}, or_3_out};  // Bit_Extender bit_extender_1
  Multiplier #(.width(32)) multiplier_1 (
    .a(Coefficient_1), .b(Coefficient_2), .out(multiplier_1_out), .cout(Overflow));  // open: cin
  or or_1 (or_1_out, and_1_out[0], and_1_out[1], and_1_out[2], and_1_out[3]);
  or or_2 (or_2_out, and_1_out[4], and_1_out[5], and_1_out[6], and_1_out[7]);
  _32bitXOR u_32bitxor_1 (
    .Input1(bit_extender_1_out), .Input2(multiplier_1_out), .Coefficient(n32bitxor_1_coefficient));
  assign Blade_Out = Blade_2 ^ Blade_1;  // XOR_Gate xor_1, 3 bits wide
  or or_3 (or_3_out, or_1_out, or_2_out);
  conditionalIncrement conditionalincrement_1 (
    .in_1(n32bitxor_1_coefficient), .Enable(or_3_out), .out_3(Coefficient_Out));
  _7_Segment_Display u_7_segment_display_1 (.g(Coefficient_Out[31]));  // open: f, a, b, e, d, c, dp
  Hex_Digit_Display hex_digit_display_1 (.value(decimalconvert_display_1_digit_10));  // open: dp
  Hex_Digit_Display hex_digit_display_2 (.value(decimalconvert_display_1_out_3));  // open: dp
  decimalconvert_display decimalconvert_display_1 (
    .Signed_Integer(Coefficient_Out), .digit_10(decimalconvert_display_1_digit_10),
    .out_3(decimalconvert_display_1_out_3), .out_4(decimalconvert_display_1_out_4),
    .out_5(decimalconvert_display_1_out_5), .out_6(decimalconvert_display_1_out_6),
    .out_7(decimalconvert_display_1_out_7), .out_8(decimalconvert_display_1_out_8),
    .out_9(decimalconvert_display_1_out_9), .out_10(decimalconvert_display_1_out_10),
    .digit_1(decimalconvert_display_1_digit_1));
  Hex_Digit_Display hex_digit_display_3 (.value(decimalconvert_display_1_out_5));  // open: dp
  Hex_Digit_Display hex_digit_display_4 (.value(decimalconvert_display_1_out_4));  // open: dp
  Hex_Digit_Display hex_digit_display_5 (.value(decimalconvert_display_1_out_6));  // open: dp
  Hex_Digit_Display hex_digit_display_6 (.value(decimalconvert_display_1_out_7));  // open: dp
  Hex_Digit_Display hex_digit_display_7 (.value(decimalconvert_display_1_out_8));  // open: dp
  Hex_Digit_Display hex_digit_display_8 (.value(decimalconvert_display_1_out_9));  // open: dp
  Hex_Digit_Display hex_digit_display_9 (.value(decimalconvert_display_1_out_10));  // open: dp
  Hex_Digit_Display hex_digit_display_10 (.value(decimalconvert_display_1_digit_1));  // open: dp
  _7_Segment_Display u_7_segment_display_2 (
    .g(1'b1), .f(1'b1), .a(1'b1), .b(1'b1), .e(1'b1), .d(1'b1), .c(1'b0), .dp(1'b0));
  _7_Segment_Display u_7_segment_display_3 (
    .g(multiplexer_3_out_6[3]), .f(multiplexer_3_out_6[2]), .a(multiplexer_3_out_6[1]),
    .b(multiplexer_3_out_6[0]), .e(multiplexer_3_out_5[3]), .d(multiplexer_3_out_5[2]),
    .c(multiplexer_3_out_5[1]), .dp(multiplexer_3_out_5[0]));
  Multiplexer #(.select(3), .width(24), .enable("false")) multiplexer_3 (
    .in0({24{1'b0}}), .in1(24'h120000), .in2(24'hbc0000), .in3(24'h12bc00), .in4(24'hb60000),
    .in5(24'hb61200), .in6(24'hbcb600), .in7(24'h12bcb6),
    .out({multiplexer_3_out_6, multiplexer_3_out_5, multiplexer_3_out_4, multiplexer_3_out_3, multiplexer_3_out_2, multiplexer_3_out}),
    .sel(Blade_Out));
  _7_Segment_Display u_7_segment_display_4 (
    .g(multiplexer_3_out_4[3]), .f(multiplexer_3_out_4[2]), .a(multiplexer_3_out_4[1]),
    .b(multiplexer_3_out_4[0]), .e(multiplexer_3_out_3[3]), .d(multiplexer_3_out_3[2]),
    .c(multiplexer_3_out_3[1]), .dp(multiplexer_3_out_3[0]));
  _7_Segment_Display u_7_segment_display_5 (
    .g(multiplexer_3_out_2[3]), .f(multiplexer_3_out_2[2]), .a(multiplexer_3_out_2[1]),
    .b(multiplexer_3_out_2[0]), .e(multiplexer_3_out[3]), .d(multiplexer_3_out[2]), .c(multiplexer_3_out[1]),
    .dp(multiplexer_3_out[0]));

  // Notes on the sheet:
  //   Will be 0 if positive, nonzero if negative
  //   e123
  //   e23
  //   e31
  //   e3
  //   e12
  //   e2
  //   e1
  //   e0
endmodule

module _5_to_32_Decoder (
  input  s4,
  input  s3,
  input  s2,
  input  s1,
  input  s0,
  output [31:0] out_6
);

  wire not_1_out, not_2_out, not_3_out, not_4_out, not_5_out;

  not not_1 (not_1_out, s4);
  not not_2 (not_2_out, s2);
  not not_3 (not_3_out, s3);
  not not_4 (not_4_out, s1);
  not not_5 (not_5_out, s0);
  and _0 (out_6[0], not_5_out, not_4_out, not_2_out, not_3_out, not_1_out);
  and _1 (out_6[1], s0, not_4_out, not_2_out, not_3_out, not_1_out);
  and _2 (out_6[2], not_5_out, s1, not_2_out, not_3_out, not_1_out);
  and _3 (out_6[3], s0, s1, not_2_out, not_3_out, not_1_out);
  and _4 (out_6[4], not_5_out, not_4_out, s2, not_3_out, not_1_out);
  and _5 (out_6[5], s0, not_4_out, s2, not_3_out, not_1_out);
  and _6 (out_6[6], not_5_out, s1, s2, not_3_out, not_1_out);
  and _7 (out_6[7], s0, s1, s2, not_3_out, not_1_out);
  and _8 (out_6[8], not_5_out, not_4_out, not_2_out, s3, not_1_out);
  and _9 (out_6[9], s0, not_4_out, not_2_out, s3, not_1_out);
  and _10 (out_6[10], not_5_out, s1, not_2_out, s3, not_1_out);
  and _11 (out_6[11], s0, s1, not_2_out, s3, not_1_out);
  and _12 (out_6[12], not_5_out, not_4_out, s2, s3, not_1_out);
  and _13 (out_6[13], s0, not_4_out, s2, s3, not_1_out);
  and _14 (out_6[14], not_5_out, s1, s2, s3, not_1_out);
  and _15 (out_6[15], s0, s1, s2, s3, not_1_out);
  and _16 (out_6[16], not_5_out, not_4_out, not_2_out, not_3_out, s4);
  and _17 (out_6[17], s0, not_4_out, not_2_out, not_3_out, s4);
  and _18 (out_6[18], not_5_out, s1, not_2_out, not_3_out, s4);
  and _19 (out_6[19], s0, s1, not_2_out, not_3_out, s4);
  and _20 (out_6[20], not_5_out, not_4_out, s2, not_3_out, s4);
  and _21 (out_6[21], s0, not_4_out, s2, not_3_out, s4);
  and _22 (out_6[22], not_5_out, s1, s2, not_3_out, s4);
  and _23 (out_6[23], s0, s1, s2, not_3_out, s4);
  and _24 (out_6[24], not_5_out, not_4_out, not_2_out, s3, s4);
  and _25 (out_6[25], s0, not_4_out, not_2_out, s3, s4);
  and _26 (out_6[26], not_5_out, s1, not_2_out, s3, s4);
  and _27 (out_6[27], s0, s1, not_2_out, s3, s4);
  and _28 (out_6[28], not_5_out, not_4_out, s2, s3, s4);
  and _29 (out_6[29], s0, not_4_out, s2, s3, s4);
  and _30 (out_6[30], not_5_out, s1, s2, s3, s4);
  and _31 (out_6[31], s0, s1, s2, s3, s4);

  // Notes on the sheet:
  //   Least Significant Bit
  //   Output
endmodule

module conditionalIncrement (
  input  [31:0] in_1,
  input  Enable,
  output [31:0] out_3
);

  wire and_1_out, and_2_out, and_3_out, and_4_out, and_5_out, and_6_out, and_7_out, and_8_out, and_9_out,
       and_10_out, and_11_out, and_12_out, and_13_out, and_14_out, and_15_out, and_16_out, and_17_out,
       and_18_out, and_19_out, and_20_out, and_21_out, and_22_out, and_23_out, and_24_out, and_25_out,
       and_26_out, and_27_out, and_28_out, and_29_out, and_30_out, and_31_out, and_32_out, not_1_out,
       not_2_out, not_3_out, not_4_out, not_5_out, not_6_out, not_7_out, not_8_out, not_9_out, not_10_out,
       not_11_out, not_12_out, not_13_out, not_14_out, not_15_out, not_16_out, not_17_out, not_18_out,
       not_19_out, not_20_out, not_21_out, not_22_out, not_23_out, not_24_out, not_25_out, not_26_out,
       not_27_out, not_28_out, not_29_out, not_30_out, not_31_out, not_32_out, not_33_out;
  wire [31:0] bit_extender_1_out, xor_5_out;

  and and_1 (and_1_out, not_2_out, in_1[22]);
  xor xor_1 (xor_5_out[23], in_1[23], and_1_out);
  not not_1 (not_1_out, xor_5_out[23]);
  not not_2 (not_2_out, xor_5_out[22]);
  xor xor_2 (xor_5_out[22], and_3_out, in_1[22]);
  and and_2 (and_2_out, not_1_out, in_1[23]);
  xor xor_3 (xor_5_out[13], in_1[13], and_5_out);
  and and_3 (and_3_out, not_7_out, in_1[21]);
  xor xor_4 (xor_5_out[24], and_2_out, in_1[24]);
  not not_3 (not_3_out, xor_5_out[24]);
  xor xor_5 (xor_5_out[0], Enable, in_1[0]);
  xor xor_6 (xor_5_out[6], in_1[6], and_9_out);
  not not_4 (not_4_out, xor_5_out[6]);
  and and_4 (and_4_out, not_4_out, in_1[6]);
  not not_5 (not_5_out, xor_5_out[12]);
  and and_5 (and_5_out, not_5_out, in_1[12]);
  and and_6 (and_6_out, in_1[13], not_6_out);
  not not_6 (not_6_out, xor_5_out[13]);
  xor xor_7 (xor_5_out[21], and_10_out, in_1[21]);
  not not_7 (not_7_out, xor_5_out[21]);
  and and_7 (and_7_out, not_3_out, in_1[24]);
  xor xor_8 (xor_5_out[25], and_7_out, in_1[25]);
  not not_8 (not_8_out, xor_5_out[0]);
  and and_8 (and_8_out, not_8_out, in_1[0]);
  and and_9 (and_9_out, in_1[5], not_9_out);
  xor xor_9 (xor_5_out[5], in_1[5], and_12_out);
  not not_9 (not_9_out, xor_5_out[5]);
  xor xor_10 (xor_5_out[7], in_1[7], and_4_out);
  xor xor_11 (xor_5_out[12], in_1[12], and_14_out);
  xor xor_12 (xor_5_out[14], and_6_out, in_1[14]);
  and and_10 (and_10_out, not_14_out, in_1[20]);
  not not_10 (not_10_out, xor_5_out[25]);
  and and_11 (and_11_out, not_10_out, in_1[25]);
  xor xor_13 (xor_5_out[1], and_8_out, in_1[1]);
  and and_12 (and_12_out, in_1[4], not_16_out);
  and and_13 (and_13_out, in_1[7], not_11_out);
  not not_11 (not_11_out, xor_5_out[7]);
  and and_14 (and_14_out, in_1[11], not_12_out);
  not not_12 (not_12_out, xor_5_out[11]);
  and and_15 (and_15_out, in_1[14], not_13_out);
  not not_13 (not_13_out, xor_5_out[14]);
  xor xor_14 (xor_5_out[20], and_18_out, in_1[20]);
  not not_14 (not_14_out, xor_5_out[20]);
  xor xor_15 (xor_5_out[26], and_11_out, in_1[26]);
  not not_15 (not_15_out, xor_5_out[1]);
  and and_16 (and_16_out, not_15_out, in_1[1]);
  xor xor_16 (xor_5_out[4], in_1[4], and_23_out);
  not not_16 (not_16_out, xor_5_out[4]);
  xor xor_17 (xor_5_out[8], and_13_out, in_1[8]);
  and and_17 (and_17_out, in_1[10], not_22_out);
  xor xor_18 (xor_5_out[11], in_1[11], and_17_out);
  xor xor_19 (xor_5_out[15], and_15_out, in_1[15]);
  not not_17 (not_17_out, xor_5_out[15]);
  not not_18 (not_18_out, xor_5_out[19]);
  and and_18 (and_18_out, not_18_out, in_1[19]);
  not not_19 (not_19_out, xor_5_out[26]);
  and and_19 (and_19_out, not_19_out, in_1[26]);
  not not_20 (not_20_out, xor_5_out[2]);
  xor xor_20 (xor_5_out[2], and_16_out, in_1[2]);
  not not_21 (not_21_out, xor_5_out[8]);
  and and_20 (and_20_out, not_21_out, in_1[8]);
  xor xor_21 (xor_5_out[10], in_1[10], and_27_out);
  not not_22 (not_22_out, xor_5_out[10]);
  and and_21 (and_21_out, not_17_out, in_1[15]);
  xor xor_22 (xor_5_out[19], and_25_out, in_1[19]);
  not not_23 (not_23_out, xor_5_out[27]);
  xor xor_23 (xor_5_out[27], and_19_out, in_1[27]);
  and and_22 (and_22_out, not_20_out, in_1[2]);
  xor xor_24 (xor_5_out[3], in_1[3], and_22_out);
  not not_24 (not_24_out, xor_5_out[3]);
  and and_23 (and_23_out, in_1[3], not_24_out);
  xor xor_25 (xor_5_out[9], and_20_out, in_1[9]);
  not not_25 (not_25_out, xor_5_out[9]);
  not not_26 (not_26_out, xor_5_out[16]);
  xor xor_26 (xor_5_out[16], and_21_out, in_1[16]);
  and and_24 (and_24_out, not_26_out, in_1[16]);
  not not_27 (not_27_out, xor_5_out[18]);
  and and_25 (and_25_out, not_27_out, in_1[18]);
  and and_26 (and_26_out, not_23_out, in_1[27]);
  and and_27 (and_27_out, in_1[9], not_25_out);
  xor xor_27 (xor_5_out[17], and_24_out, in_1[17]);
  and and_28 (and_28_out, in_1[17], not_29_out);
  xor xor_28 (xor_5_out[18], and_28_out, in_1[18]);
  xor xor_29 (xor_5_out[28], and_26_out, in_1[28]);
  not not_28 (not_28_out, xor_5_out[28]);
  and and_29 (and_29_out, not_28_out, in_1[28]);
  not not_29 (not_29_out, xor_5_out[17]);
  xor xor_30 (xor_5_out[29], and_29_out, in_1[29]);
  not not_30 (not_30_out, xor_5_out[29]);
  and and_30 (and_30_out, not_30_out, in_1[29]);
  xor xor_31 (xor_5_out[30], in_1[30], and_30_out);
  not not_31 (not_31_out, xor_5_out[30]);
  and and_31 (and_31_out, in_1[30], not_31_out);
  xor xor_32 (xor_5_out[31], in_1[31], and_31_out);
  not not_32 (not_32_out, and_32_out);
  not not_33 (not_33_out, xor_5_out[31]);
  and and_32 (and_32_out, not_33_out, in_1[31]);
  assign out_3 = xor_5_out & bit_extender_1_out;  // AND_Gate and_33, 32 bits wide
  assign bit_extender_1_out = {{31{not_32_out}}, not_32_out};  // Bit_Extender bit_extender_1

  // Notes on the sheet:
  //   32 bit coefficient
endmodule

// display_circuit
module display (
  input  [2:0] Blade,
  input  [31:0] Coefficient
);

  wire [3:0] decimalconvert_display_1_digit_1, decimalconvert_display_1_digit_10,
       decimalconvert_display_1_out_3, decimalconvert_display_1_out_4, decimalconvert_display_1_out_5,
       decimalconvert_display_1_out_6, decimalconvert_display_1_out_7, decimalconvert_display_1_out_8,
       decimalconvert_display_1_out_9, decimalconvert_display_1_out_10, multiplexer_1_out;
  wire [23:4] multiplexer_1_out_2;

  _7_Segment_Display u_7_segment_display_1 (.g(Coefficient[31]));  // open: f, a, b, e, d, c, dp
  Hex_Digit_Display hex_digit_display_1 (.value(decimalconvert_display_1_digit_10));  // open: dp
  Hex_Digit_Display hex_digit_display_2 (.value(decimalconvert_display_1_out_4));  // open: dp
  Hex_Digit_Display hex_digit_display_3 (.value(decimalconvert_display_1_out_3));  // open: dp
  decimalconvert_display decimalconvert_display_1 (
    .Signed_Integer(Coefficient), .digit_10(decimalconvert_display_1_digit_10),
    .out_3(decimalconvert_display_1_out_3), .out_4(decimalconvert_display_1_out_4),
    .out_5(decimalconvert_display_1_out_5), .out_6(decimalconvert_display_1_out_6),
    .out_7(decimalconvert_display_1_out_7), .out_8(decimalconvert_display_1_out_8),
    .out_9(decimalconvert_display_1_out_9), .out_10(decimalconvert_display_1_out_10),
    .digit_1(decimalconvert_display_1_digit_1));
  Hex_Digit_Display hex_digit_display_4 (.value(decimalconvert_display_1_out_5));  // open: dp
  Hex_Digit_Display hex_digit_display_5 (.value(decimalconvert_display_1_out_6));  // open: dp
  Hex_Digit_Display hex_digit_display_6 (.value(decimalconvert_display_1_out_7));  // open: dp
  Hex_Digit_Display hex_digit_display_7 (.value(decimalconvert_display_1_out_8));  // open: dp
  Hex_Digit_Display hex_digit_display_8 (.value(decimalconvert_display_1_out_9));  // open: dp
  Hex_Digit_Display hex_digit_display_9 (.value(decimalconvert_display_1_out_10));  // open: dp
  Hex_Digit_Display hex_digit_display_10 (.value(decimalconvert_display_1_digit_1));  // open: dp
  _7_Segment_Display u_7_segment_display_2 (
    .g(1'b1), .f(1'b1), .a(1'b1), .b(1'b1), .e(1'b1), .d(1'b1), .c(1'b0), .dp(1'b0));
  _7_Segment_Display u_7_segment_display_3 (
    .g(multiplexer_1_out_2[23]), .f(multiplexer_1_out_2[22]), .a(multiplexer_1_out_2[21]),
    .b(multiplexer_1_out_2[20]), .e(multiplexer_1_out_2[19]), .d(multiplexer_1_out_2[18]),
    .c(multiplexer_1_out_2[17]), .dp(multiplexer_1_out_2[16]));
  Multiplexer #(.select(3), .width(24), .enable("false")) multiplexer_1 (
    .in0({24{1'b0}}), .in1(24'h120000), .in2(24'hbc0000), .in3(24'h12bc00), .in4(24'hb60000),
    .in5(24'hb61200), .in6(24'hbcb600), .in7(24'h12bcb6), .out({multiplexer_1_out_2, multiplexer_1_out}),
    .sel(Blade));
  _7_Segment_Display u_7_segment_display_4 (
    .g(multiplexer_1_out_2[15]), .f(multiplexer_1_out_2[14]), .a(multiplexer_1_out_2[13]),
    .b(multiplexer_1_out_2[12]), .e(multiplexer_1_out_2[11]), .d(multiplexer_1_out_2[10]),
    .c(multiplexer_1_out_2[9]), .dp(multiplexer_1_out_2[8]));
  _7_Segment_Display u_7_segment_display_5 (
    .g(multiplexer_1_out_2[7]), .f(multiplexer_1_out_2[6]), .a(multiplexer_1_out_2[5]),
    .b(multiplexer_1_out_2[4]), .e(multiplexer_1_out[3]), .d(multiplexer_1_out[2]), .c(multiplexer_1_out[1]),
    .dp(multiplexer_1_out[0]));

  // Notes on the sheet:
  //   e123
  //   e23
  //   e31
  //   e3
  //   e12
  //   e2
  //   e1
  //   e0
endmodule

// decimalconverter
module decimalconvert_display (
  input  [31:0] Signed_Integer,
  output [3:0] digit_10,
  output [3:0] out_3,
  output [3:0] out_4,
  output [3:0] out_5,
  output [3:0] out_6,
  output [3:0] out_7,
  output [3:0] out_8,
  output [3:0] out_9,
  output [3:0] out_10,
  output [3:0] digit_1
);

  wire clock_1_out;
  wire [3:0] divider_1_rem, divider_1_rem_2, divider_1_rem_3, divider_1_rem_4, divider_1_rem_5,
       divider_1_rem_6, divider_1_rem_7;
  wire [31:0] bit_extender_1_out, conditionalincrement_1_out_3, divider_1_out, divider_2_out, divider_3_out,
       divider_4_out, divider_5_out, divider_6_out, divider_7_out, divider_8_out, divider_10_out,
       multiplexer_1_out, xor_1_out;
  wire [31:4] divider_2_rem, divider_3_rem, divider_4_rem, divider_5_rem, divider_6_rem, divider_7_rem,
       divider_8_rem, divider_9_rem, divider_10_rem;

  Clock clock_1 (.out(clock_1_out));
  assign xor_1_out = Signed_Integer ^ bit_extender_1_out;  // XOR_Gate xor_1, 32 bits wide
  conditionalIncrement conditionalincrement_1 (
    .in_1(xor_1_out), .Enable(Signed_Integer[31]), .out_3(conditionalincrement_1_out_3));
  Multiplexer #(.width(32), .enable("false")) multiplexer_1 (
    .in0(multiplexer_1_out), .in1(conditionalincrement_1_out_3), .out(multiplexer_1_out), .sel(clock_1_out));
  Divider #(.width(32)) divider_1 (
    .a(multiplexer_1_out), .b(32'ha), .out(divider_1_out),
    .rem({divider_1_rem_7, divider_1_rem_6, divider_1_rem_5, divider_1_rem_4, divider_1_rem_3, divider_1_rem_2, divider_1_rem, digit_1}));  // open: upper
  assign bit_extender_1_out = {{31{Signed_Integer[31]}}, Signed_Integer[31]};  // Bit_Extender bit_extender_1
  Divider #(.width(32)) divider_2 (
    .a(divider_1_out), .b(32'ha), .out(divider_2_out), .rem({divider_2_rem, out_10}));  // open: upper
  Divider #(.width(32)) divider_3 (
    .a(divider_2_out), .b(32'ha), .out(divider_3_out), .rem({divider_3_rem, out_9}));  // open: upper
  Divider #(.width(32)) divider_4 (
    .a(divider_3_out), .b(32'ha), .out(divider_4_out), .rem({divider_4_rem, out_8}));  // open: upper
  Divider #(.width(32)) divider_5 (
    .a(divider_4_out), .b(32'ha), .out(divider_5_out), .rem({divider_5_rem, out_7}));  // open: upper
  Divider #(.width(32)) divider_6 (
    .a(divider_5_out), .b(32'ha), .out(divider_6_out), .rem({divider_6_rem, out_6}));  // open: upper
  Divider #(.width(32)) divider_7 (
    .a(divider_6_out), .b(32'ha), .out(divider_7_out), .rem({divider_7_rem, out_5}));  // open: upper
  Divider #(.width(32)) divider_8 (
    .a(divider_7_out), .b(32'ha), .out(divider_8_out), .rem({divider_8_rem, out_4}));  // open: upper
  Divider #(.width(32)) divider_9 (.a(divider_10_out), .b(32'ha), .rem({divider_9_rem, digit_10}));  // open: out, upper
  Divider #(.width(32)) divider_10 (
    .a(divider_8_out), .b(32'ha), .out(divider_10_out), .rem({divider_10_rem, out_3}));  // open: upper
endmodule

module _32bitXOR (
  input  [31:0] Input1,
  input  [31:0] Input2,
  output [31:0] Coefficient
);

  xor xor_1 (Coefficient[0], Input1[0], Input2[0]);
  xor xor_2 (Coefficient[1], Input1[1], Input2[1]);
  xor xor_3 (Coefficient[2], Input1[2], Input2[2]);
  xor xor_4 (Coefficient[3], Input1[3], Input2[3]);
  xor xor_5 (Coefficient[8], Input1[8], Input2[8]);
  xor xor_6 (Coefficient[9], Input1[9], Input2[9]);
  xor xor_7 (Coefficient[10], Input1[10], Input2[10]);
  xor xor_8 (Coefficient[11], Input1[11], Input2[11]);
  xor xor_9 (Coefficient[12], Input1[12], Input2[12]);
  xor xor_10 (Coefficient[13], Input1[13], Input2[13]);
  xor xor_11 (Coefficient[14], Input1[14], Input2[14]);
  xor xor_12 (Coefficient[15], Input1[15], Input2[15]);
  xor xor_13 (Coefficient[16], Input1[16], Input2[16]);
  xor xor_14 (Coefficient[17], Input1[17], Input2[17]);
  xor xor_15 (Coefficient[18], Input1[18], Input2[18]);
  xor xor_16 (Coefficient[19], Input1[19], Input2[19]);
  xor xor_17 (Coefficient[20], Input1[20], Input2[20]);
  xor xor_18 (Coefficient[21], Input1[21], Input2[21]);
  xor xor_19 (Coefficient[22], Input1[22], Input2[22]);
  xor xor_20 (Coefficient[23], Input1[23], Input2[23]);
  xor xor_21 (Coefficient[24], Input1[24], Input2[24]);
  xor xor_22 (Coefficient[25], Input1[25], Input2[25]);
  xor xor_23 (Coefficient[26], Input1[26], Input2[26]);
  xor xor_24 (Coefficient[27], Input1[27], Input2[27]);
  xor xor_25 (Coefficient[28], Input1[28], Input2[28]);
  xor xor_26 (Coefficient[29], Input1[29], Input2[29]);
  xor xor_27 (Coefficient[30], Input1[30], Input2[30]);
  xor xor_28 (Coefficient[31], Input1[31], Input2[31]);
  xor xor_29 (Coefficient[4], Input1[4], Input2[4]);
  xor xor_30 (Coefficient[5], Input1[5], Input2[5]);
  xor xor_31 (Coefficient[6], Input1[6], Input2[6]);
  xor xor_32 (Coefficient[7], Input1[7], Input2[7]);
endmodule
